// Logisim project TUCE_V1_.circ as structural Verilog: 9 circuits, main circuit main
module main (
  input  HOLD,
  input  RESET,
  input  DT_WRAP,
  input  PC_WRAP,
  input  MP_WRAP,
  output [7:0] out_6,
  output [15:0] DEPTH
);

  wire clock_1_out, keyboard_1_avail, or_1_out, tuce_v1_1_input_read, tuce_v1_1_s1, tuce_v1_1_s2,
       tuce_v1_1_s3, tuce_v1_1_s4, tuce_v1_1_write_memory, tuce_v1_1_write_output;
  wire [6:0] keyboard_1_data;
  wire [7:0] ram_1_dout, rom_1_data, tuce_v1_1_memory_out;
  wire [15:0] tuce_v1_1_mem_addr, tuce_v1_1_prg_addr;

  or or_1 (or_1_out, HOLD, keyboard_1_avail);
  Clock clock_1 (.out(clock_1_out));
  Keyboard #(.buflen(256)) keyboard_1 (
    .clk(tuce_v1_1_input_read), .re(1'b1), .clr(RESET), .avail(keyboard_1_avail), .data(keyboard_1_data));
  ROM #(.addrWidth(16)) rom_1 (.addr(tuce_v1_1_prg_addr), .data(rom_1_data));
  RAM #(.addrWidth(16)) ram_1 (
    .addr(tuce_v1_1_mem_addr), .we(tuce_v1_1_write_memory), .oe(1'b1), .clk(clock_1_out),
    .din(tuce_v1_1_memory_out), .dout(ram_1_dout));
  LED led_1 (.in(tuce_v1_1_input_read));
  TUCE_V1 tuce_v1_1 (
    .INPUT({1'b0, keyboard_1_data}), .MEMORY_IN(ram_1_dout), .INSTRUCTION(rom_1_data), .RESET(RESET),
    .CLOCK(clock_1_out), .HOLD(or_1_out), .ENABLE_DT_WRAPPING(DT_WRAP), .ENABLE_PC_WRAPPING(PC_WRAP),
    .ENABLE_MP_WRAPPING(MP_WRAP), .INPUT_READ(tuce_v1_1_input_read), .S1(tuce_v1_1_s1), .S2(tuce_v1_1_s2),
    .S3(tuce_v1_1_s3), .S4(tuce_v1_1_s4), .WRITE_OUTPUT(tuce_v1_1_write_output), .OUTPUT(out_6),
    .WRITE_MEMORY(tuce_v1_1_write_memory), .MEMORY_OUT(tuce_v1_1_memory_out), .MEM_ADDR(tuce_v1_1_mem_addr),
    .PRG_ADDR(tuce_v1_1_prg_addr), .DEPTH(DEPTH));
  LED led_2 (.in(tuce_v1_1_s1));
  LED led_3 (.in(tuce_v1_1_s2));
  LED led_4 (.in(tuce_v1_1_s3));
  LED led_5 (.in(tuce_v1_1_s4));
  LED led_6 (.in(tuce_v1_1_write_output));
  TTY #(.rows(16)) tty_1 (.data(out_6[6:0]), .clk(tuce_v1_1_write_output), .we(1'b1), .clr(RESET));

  // Notes on the sheet:
  //   contents of rom_1 (hex, n*v repeats v):
  //   1 1 1 8 1 4 1 5*4 1 10*4 40 40 1 1 1 4 2 2 2 8 80 1 5*4 1 4 1 1 4 40 2 2 4 5*1 4 2 2 2 8 80 2 8 80
  //   4*1 40 40 1 1 1 4 1 4 4*2 8 80 4 4 4 1 1 4 40 2 4 1 1 1 4 1 4 2 2 2 8 80 1 1 40 1 40 40 1 1 1 4 2 2
  //   2 8 80 2 80 2 2 4 4 1 4 6*1 8 80 2 8 80 4 4 4 1 4 1 40 40 8 80 2 4 2 40 1 17*4 2 8 80 2 4 80 1 1 40
  //   40 9*4 10 8*8 1 1 1 80 4 40 8 2 2 2 80 1 1 1 40 1 1 20 10*8 40 1 80 2 80 2 2 40 2 2 2 40 1 8 8 40 2
  //   8 1 1 4 1 8 2 2 8 80 2 40 40 1 1 1 80 4 1 8 40 4 1 1 4 1 8 80 4 40 2 2 2 80 2 8 80 1 4 4 1 40 2 4 1
  //   8 80 1 40 40 1 1 1 80 4 40 2 2 2 80 1 1 1 8 80 4 40 8 1 1 1 80 2 8 40 4 4 1 80 1 40 6*8 2 80 1 4 4 4
  //   40 2 2 2 80 1 80 2 80 1 40 8 40 4 1 1 4 1 8 80 4 1 1 4 1 1 1 4 1 40 2 2 2 80 1 8 1 4 1 40 1 40 8 1 4
  //   1 4 4 4 1 1 4 4 40 1 1 1 80 4 4 4 2 2 2 4 4 2 2 2 4 4 40 1 1 1 80 1 1 1 80 2 2 2 40 1 40 1 1 1 80 4
  //   1 1 1 80 7*2 40 2 2 4 4 2 4 40 8 2 2 2 4 80 8 1 4 4 1 1 1 4 4 1 1 1 4 4 4*2 80 2 2 2 4 40 8 2 2 2 4
  //   80 4 1 8 1 1 8 1 1 80 2 2 4 2 2 4 2 2 2 4 2 2 8 40 4 2 4 2 2 8 80 4 2 4 40 8 1 4 1 40 8 2 8 2 2 40 2
  //   2 2 80 1 40 1 1 40 1 1 1 80 2 2 4 2 40 2 2 2 80 1 8 80 80 2 40 2 40 2 40 2 2 2 80 1 4 1 1 40 1 1 1
  //   80 2 2 8 80 2 40 2 2 2 80 80 1 1 1 8 1 1 1 40 1 1 1 80 4 1 80 1 4 40 8 2 2 40 8 80 2 80 8 40 40 1 1
  //   1 80 2 40 2 2 40 2 2 2 80 5*1 4 1 40 1 1 1 80 2 8 80 1 1 1 40 1 40 1 1 1 80 4*2 4 1 40 2 2 2 80 1 1
  //   8 80 1 80 6*2 40 8 8 8 2 5*8 40 8 40 8 40 2 8 1 1 4 4 4 2 7*4 40 8 4*80 2 4 2 4 80 1 80 1 1 80
endmodule

module IDU (
  input  DEC,
  input  [7:0] DATA_IN,
  output [7:0] DATA_OUT
);

  wire decrement_cell_1_co, decrement_cell_2_co, decrement_cell_3_co, decrement_cell_4_co,
       decrement_cell_5_co, decrement_cell_6_co, decrement_cell_7_co, half_adder_1_c, half_adder_2_c,
       half_adder_3_c, half_adder_4_c, half_adder_5_c, half_adder_6_c, half_adder_7_c, not_1_out;
  wire [7:0] decrement_cell_1_s, half_adder_1_s;

  not not_1 (not_1_out, DEC);
  Decrement_Cell decrement_cell_1 (.CI(1'b0), .D(DATA_IN[0]), .S(decrement_cell_1_s[0]), .CO(decrement_cell_1_co));
  Decrement_Cell decrement_cell_2 (
    .CI(decrement_cell_1_co), .D(DATA_IN[1]), .S(decrement_cell_1_s[1]), .CO(decrement_cell_2_co));
  Decrement_Cell decrement_cell_3 (
    .CI(decrement_cell_2_co), .D(DATA_IN[2]), .S(decrement_cell_1_s[2]), .CO(decrement_cell_3_co));
  Decrement_Cell decrement_cell_4 (
    .CI(decrement_cell_3_co), .D(DATA_IN[3]), .S(decrement_cell_1_s[3]), .CO(decrement_cell_4_co));
  Decrement_Cell decrement_cell_5 (
    .CI(decrement_cell_4_co), .D(DATA_IN[4]), .S(decrement_cell_1_s[4]), .CO(decrement_cell_5_co));
  Decrement_Cell decrement_cell_6 (
    .CI(decrement_cell_5_co), .D(DATA_IN[5]), .S(decrement_cell_1_s[5]), .CO(decrement_cell_6_co));
  Decrement_Cell decrement_cell_7 (
    .CI(decrement_cell_6_co), .D(DATA_IN[6]), .S(decrement_cell_1_s[6]), .CO(decrement_cell_7_co));
  Decrement_Cell decrement_cell_8 (.CI(decrement_cell_7_co), .D(DATA_IN[7]), .S(decrement_cell_1_s[7]));  // open: CO
  assign DATA_OUT = DEC ? decrement_cell_1_s : 8'bz;  // Controlled_Buffer controlled_buffer_1
  Half_Adder half_adder_1 (.A(1'b1), .B(DATA_IN[0]), .S(half_adder_1_s[0]), .C(half_adder_1_c));
  Half_Adder half_adder_2 (.A(half_adder_1_c), .B(DATA_IN[1]), .S(half_adder_1_s[1]), .C(half_adder_2_c));
  Half_Adder half_adder_3 (.A(half_adder_2_c), .B(DATA_IN[2]), .S(half_adder_1_s[2]), .C(half_adder_3_c));
  Half_Adder half_adder_4 (.A(half_adder_3_c), .B(DATA_IN[3]), .S(half_adder_1_s[3]), .C(half_adder_4_c));
  Half_Adder half_adder_5 (.A(half_adder_4_c), .B(DATA_IN[4]), .S(half_adder_1_s[4]), .C(half_adder_5_c));
  Half_Adder half_adder_6 (.A(half_adder_5_c), .B(DATA_IN[5]), .S(half_adder_1_s[5]), .C(half_adder_6_c));
  Half_Adder half_adder_7 (.A(half_adder_6_c), .B(DATA_IN[6]), .S(half_adder_1_s[6]), .C(half_adder_7_c));
  Half_Adder half_adder_8 (.A(half_adder_7_c), .B(DATA_IN[7]), .S(half_adder_1_s[7]));  // open: C
  assign DATA_OUT = not_1_out ? half_adder_1_s : 8'bz;  // Controlled_Buffer controlled_buffer_2
endmodule

module Half_Adder (
  input  A,
  input  B,
  output S,
  output C
);

  xor xor_1 (S, A, B);
  and and_1 (C, A, B);
endmodule

module Decrement_Cell (
  input  CI,
  input  D,
  output S,
  output CO
);

  wire not_1_out;

  or or_1 (CO, D, CI);
  not not_1 (not_1_out, D);
  xor xor_1 (S, not_1_out, CI);
endmodule

module TUCE_V1 (
  input  [7:0] INPUT,
  input  [7:0] MEMORY_IN,
  input  [7:0] INSTRUCTION,
  input  RESET,
  input  CLOCK,
  input  HOLD,
  input  ENABLE_DT_WRAPPING,
  input  ENABLE_PC_WRAPPING,
  input  ENABLE_MP_WRAPPING,
  output INPUT_READ,
  output S1,
  output S2,
  output S3,
  output S4,
  output WRITE_OUTPUT,
  output [7:0] OUTPUT,
  output WRITE_MEMORY,
  output [7:0] MEMORY_OUT,
  output [15:0] MEM_ADDR,
  output [15:0] PRG_ADDR,
  output [15:0] DEPTH
);

  wire and_1_out, and_2_out, and_3_out, and_5_out, and_6_out, and_7_out, and_8_out, and_9_out, and_10_out,
       and_11_out, and_12_out, and_13_out, and_14_out, and_15_out, and_16_out, and_17_out, BLF_q, DT_zero,
       FLF_q, MP_zero, nor_1_out, nor_2_out, nor_3_out, not_1_out, not_2_out, not_3_out, not_4_out, or_1_out,
       or_2_out, or_3_out, or_4_out, or_5_out, or_6_out, or_7_out, or_8_out, or_9_out, or_10_out, PC_zero;
  wire [1:0] SC_value;
  wire [7:0] controlled_buffer_1_out, idu_1_data_out, INR_q, IR_q, MIR_q;

  and and_1 (and_1_out, ~nor_1_out, CLOCK);  // AND_Gate
  nor nor_1 (nor_1_out, and_1_out, HOLD);
  not not_1 (not_1_out, and_1_out);
  and and_2 (and_2_out, S4, and_1_out);
  or or_1 (or_1_out, and_2_out, RESET);
  Register INR (.D(INPUT), .en(INPUT_READ), .clk(not_1_out), .Q(INR_q), .clr(or_1_out));
  Register MIR (.D(MEMORY_IN), .en(and_3_out), .clk(not_1_out), .Q(MIR_q), .clr(or_1_out));
  Register IR (.D(INSTRUCTION), .en(S1), .clk(and_1_out), .Q(IR_q), .clr(or_1_out));
  Stage_Counter SC (.CLOCK(not_1_out), .RESET(RESET), .VALUE(SC_value));
  Decoder #(.enable("false"), .select(2)) decoder_1 (.out0(S1), .out1(S2), .out2(S3), .out3(S4), .sel(SC_value));
  assign controlled_buffer_1_out = IR_q[5] ? INR_q : 8'bz;  // Controlled_Buffer controlled_buffer_1
  and and_3 (and_3_out, S1, nor_3_out, or_2_out);
  and and_4 (INPUT_READ, S1, nor_3_out, IR_q[5]);
  and and_5 (and_5_out, S1, nor_3_out, or_3_out);
  or or_2 (or_2_out, IR_q[2], IR_q[3], IR_q[4], IR_q[6], IR_q[7]);
  or or_3 (or_3_out, IR_q[0], IR_q[1]);
  or or_4 (or_4_out, IR_q[2], IR_q[3]);
  not not_2 (not_2_out, IR_q[1]);
  nor nor_2 (nor_2_out, MIR_q[0], MIR_q[1], MIR_q[2], MIR_q[3], MIR_q[4], MIR_q[5], MIR_q[6], MIR_q[7]);
  IDU idu_1 (.DEC(IR_q[3]), .DATA_IN(MIR_q), .DATA_OUT(idu_1_data_out));
  assign controlled_buffer_1_out = or_4_out ? idu_1_data_out : 8'bz;  // Controlled_Buffer controlled_buffer_2
  and and_6 (and_6_out, IR_q[6], nor_2_out, S2);
  and and_7 (and_7_out, IR_q[7], ~nor_2_out, S2);  // AND_Gate
  and and_8 (and_8_out, and_1_out, nor_3_out, and_6_out);
  not not_3 (not_3_out, and_6_out);
  and and_9 (and_9_out, not_3_out, nor_3_out, and_1_out);
  and and_10 (and_10_out, and_1_out, nor_3_out, and_7_out);
  not not_4 (not_4_out, and_7_out);
  and and_11 (and_11_out, not_4_out, nor_3_out, and_1_out);
  and and_12 (and_12_out, FLF_q, IR_q[6]);
  and and_13 (and_13_out, BLF_q, IR_q[7]);
  or or_5 (or_5_out, IR_q[6], IR_q[7]);
  or or_6 (or_6_out, and_9_out, RESET, and_15_out);
  or or_7 (or_7_out, and_11_out, RESET, and_15_out);
  or or_8 (or_8_out, and_12_out, and_13_out);
  and and_14 (and_14_out, ~nor_3_out, S2, or_5_out);  // AND_Gate
  SR_Latch FLF (.S(and_8_out), .R(or_6_out), .Q(FLF_q));
  SR_Latch BLF (.S(and_10_out), .R(or_7_out), .Q(BLF_q));
  and and_15 (and_15_out, ~nor_3_out, DT_zero, and_1_out, S3);  // AND_Gate
  nor nor_3 (nor_3_out, FLF_q, BLF_q);
  or or_9 (or_9_out, nor_3_out, FLF_q);
  TUCE_Counter DT (
    .RESET(RESET), .ENABLE(and_14_out), .UP_DOWN(or_8_out), .WRAP(ENABLE_DT_WRAPPING), .CLOCK(not_1_out),
    .OUTPUT(DEPTH), .ZERO(DT_zero));
  TUCE_Counter PC (
    .RESET(RESET), .ENABLE(S4), .UP_DOWN(or_9_out), .WRAP(ENABLE_PC_WRAPPING), .CLOCK(and_1_out),
    .OUTPUT(PRG_ADDR), .ZERO(PC_zero));
  // NoConnect on PC_zero
  TUCE_Counter MP (
    .RESET(RESET), .ENABLE(and_5_out), .UP_DOWN(not_2_out), .WRAP(ENABLE_MP_WRAPPING), .CLOCK(not_1_out),
    .OUTPUT(MEM_ADDR), .ZERO(MP_zero));
  // NoConnect on MP_zero
  and and_16 (and_16_out, IR_q[4], nor_3_out, S2);
  and and_17 (and_17_out, S2, nor_3_out, or_10_out);
  or or_10 (or_10_out, IR_q[5], or_4_out);
  Register #(.width(1)) OWF (.D(1'b1), .en(and_16_out), .clk(not_1_out), .Q(WRITE_OUTPUT), .clr(or_1_out));
  Register OUTR (.D(MIR_q), .en(and_16_out), .clk(not_1_out), .Q(OUTPUT), .clr(or_1_out));
  Register #(.width(1)) MOWF (.D(1'b1), .en(and_17_out), .clk(not_1_out), .Q(WRITE_MEMORY), .clr(or_1_out));
  Register MOR (.D(controlled_buffer_1_out), .en(and_17_out), .clk(not_1_out), .Q(MEMORY_OUT), .clr(or_1_out));
endmodule

module TUCE_Counter (
  input  RESET,
  input  ENABLE,
  input  UP_DOWN,
  input  WRAP,
  input  CLOCK,
  output [15:0] OUTPUT,
  output ZERO
);

  wire and_1_out, and_2_out, and_3_out, and_4_out, counter_cell_1_b, counter_cell_1_down_out,
       counter_cell_1_up_out, counter_cell_2_b, counter_cell_2_down_out, counter_cell_2_up_out,
       counter_cell_3_b, counter_cell_3_down_out, counter_cell_3_up_out, counter_cell_4_b,
       counter_cell_4_down_out, counter_cell_4_up_out, counter_cell_5_b, counter_cell_5_down_out,
       counter_cell_5_up_out, counter_cell_6_b, counter_cell_6_down_out, counter_cell_6_up_out,
       counter_cell_7_b, counter_cell_7_down_out, counter_cell_7_up_out, counter_cell_8_b,
       counter_cell_8_down_out, counter_cell_8_up_out, counter_cell_9_b, counter_cell_9_down_out,
       counter_cell_9_up_out, counter_cell_10_b, counter_cell_10_down_out, counter_cell_10_up_out,
       counter_cell_11_b, counter_cell_11_down_out, counter_cell_11_up_out, counter_cell_12_b,
       counter_cell_12_down_out, counter_cell_12_up_out, counter_cell_13_b, counter_cell_13_down_out,
       counter_cell_13_up_out, counter_cell_14_b, counter_cell_14_down_out, counter_cell_14_up_out,
       counter_cell_15_b, counter_cell_15_down_out, counter_cell_15_up_out, nand_1_out, nand_2_out,
       not_1_out, not_2_out, or_1_out;

  not not_1 (not_1_out, UP_DOWN);
  and and_1 (and_1_out, ENABLE, CLOCK);
  nand nand_1 (nand_1_out, and_4_out, UP_DOWN);
  nand nand_2 (nand_2_out, ZERO, not_1_out);
  not not_2 (not_2_out, WRAP);
  and and_2 (and_2_out, nand_1_out, not_2_out, nand_2_out);
  Counter_Cell counter_cell_1 (
    .UP_IN(UP_DOWN), .A(1'b1), .DOWN_IN(not_1_out), .RESET(RESET), .CLOCK(and_3_out), .Q(OUTPUT[0]),
    .UP_OUT(counter_cell_1_up_out), .B(counter_cell_1_b), .DOWN_OUT(counter_cell_1_down_out));
  Counter_Cell counter_cell_2 (
    .UP_IN(counter_cell_1_up_out), .A(counter_cell_1_b), .DOWN_IN(counter_cell_1_down_out), .RESET(RESET),
    .CLOCK(and_3_out), .Q(OUTPUT[1]), .UP_OUT(counter_cell_2_up_out), .B(counter_cell_2_b),
    .DOWN_OUT(counter_cell_2_down_out));
  Counter_Cell counter_cell_3 (
    .UP_IN(counter_cell_2_up_out), .A(counter_cell_2_b), .DOWN_IN(counter_cell_2_down_out), .RESET(RESET),
    .CLOCK(and_3_out), .Q(OUTPUT[2]), .UP_OUT(counter_cell_3_up_out), .B(counter_cell_3_b),
    .DOWN_OUT(counter_cell_3_down_out));
  Counter_Cell counter_cell_4 (
    .UP_IN(counter_cell_3_up_out), .A(counter_cell_3_b), .DOWN_IN(counter_cell_3_down_out), .RESET(RESET),
    .CLOCK(and_3_out), .Q(OUTPUT[3]), .UP_OUT(counter_cell_4_up_out), .B(counter_cell_4_b),
    .DOWN_OUT(counter_cell_4_down_out));
  Counter_Cell counter_cell_5 (
    .UP_IN(counter_cell_4_up_out), .A(counter_cell_4_b), .DOWN_IN(counter_cell_4_down_out), .RESET(RESET),
    .CLOCK(and_3_out), .Q(OUTPUT[4]), .UP_OUT(counter_cell_5_up_out), .B(counter_cell_5_b),
    .DOWN_OUT(counter_cell_5_down_out));
  Counter_Cell counter_cell_6 (
    .UP_IN(counter_cell_5_up_out), .A(counter_cell_5_b), .DOWN_IN(counter_cell_5_down_out), .RESET(RESET),
    .CLOCK(and_3_out), .Q(OUTPUT[5]), .UP_OUT(counter_cell_6_up_out), .B(counter_cell_6_b),
    .DOWN_OUT(counter_cell_6_down_out));
  Counter_Cell counter_cell_7 (
    .UP_IN(counter_cell_6_up_out), .A(counter_cell_6_b), .DOWN_IN(counter_cell_6_down_out), .RESET(RESET),
    .CLOCK(and_3_out), .Q(OUTPUT[6]), .UP_OUT(counter_cell_7_up_out), .B(counter_cell_7_b),
    .DOWN_OUT(counter_cell_7_down_out));
  Counter_Cell counter_cell_8 (
    .UP_IN(counter_cell_7_up_out), .A(counter_cell_7_b), .DOWN_IN(counter_cell_7_down_out), .RESET(RESET),
    .CLOCK(and_3_out), .Q(OUTPUT[7]), .UP_OUT(counter_cell_8_up_out), .B(counter_cell_8_b),
    .DOWN_OUT(counter_cell_8_down_out));
  Counter_Cell counter_cell_9 (
    .UP_IN(counter_cell_8_up_out), .A(counter_cell_8_b), .DOWN_IN(counter_cell_8_down_out), .RESET(RESET),
    .CLOCK(and_3_out), .Q(OUTPUT[8]), .UP_OUT(counter_cell_9_up_out), .B(counter_cell_9_b),
    .DOWN_OUT(counter_cell_9_down_out));
  Counter_Cell counter_cell_10 (
    .UP_IN(counter_cell_9_up_out), .A(counter_cell_9_b), .DOWN_IN(counter_cell_9_down_out), .RESET(RESET),
    .CLOCK(and_3_out), .Q(OUTPUT[9]), .UP_OUT(counter_cell_10_up_out), .B(counter_cell_10_b),
    .DOWN_OUT(counter_cell_10_down_out));
  Counter_Cell counter_cell_11 (
    .UP_IN(counter_cell_10_up_out), .A(counter_cell_10_b), .DOWN_IN(counter_cell_10_down_out), .RESET(RESET),
    .CLOCK(and_3_out), .Q(OUTPUT[10]), .UP_OUT(counter_cell_11_up_out), .B(counter_cell_11_b),
    .DOWN_OUT(counter_cell_11_down_out));
  Counter_Cell counter_cell_12 (
    .UP_IN(counter_cell_11_up_out), .A(counter_cell_11_b), .DOWN_IN(counter_cell_11_down_out), .RESET(RESET),
    .CLOCK(and_3_out), .Q(OUTPUT[11]), .UP_OUT(counter_cell_12_up_out), .B(counter_cell_12_b),
    .DOWN_OUT(counter_cell_12_down_out));
  Counter_Cell counter_cell_13 (
    .UP_IN(counter_cell_12_up_out), .A(counter_cell_12_b), .DOWN_IN(counter_cell_12_down_out), .RESET(RESET),
    .CLOCK(and_3_out), .Q(OUTPUT[12]), .UP_OUT(counter_cell_13_up_out), .B(counter_cell_13_b),
    .DOWN_OUT(counter_cell_13_down_out));
  Counter_Cell counter_cell_14 (
    .UP_IN(counter_cell_13_up_out), .A(counter_cell_13_b), .DOWN_IN(counter_cell_13_down_out), .RESET(RESET),
    .CLOCK(and_3_out), .Q(OUTPUT[13]), .UP_OUT(counter_cell_14_up_out), .B(counter_cell_14_b),
    .DOWN_OUT(counter_cell_14_down_out));
  Counter_Cell counter_cell_15 (
    .UP_IN(counter_cell_14_up_out), .A(counter_cell_14_b), .DOWN_IN(counter_cell_14_down_out), .RESET(RESET),
    .CLOCK(and_3_out), .Q(OUTPUT[14]), .UP_OUT(counter_cell_15_up_out), .B(counter_cell_15_b),
    .DOWN_OUT(counter_cell_15_down_out));
  Counter_Cell counter_cell_16 (
    .UP_IN(counter_cell_15_up_out), .A(counter_cell_15_b), .DOWN_IN(counter_cell_15_down_out), .RESET(RESET),
    .CLOCK(and_3_out), .Q(OUTPUT[15]));  // open: UP_OUT, B, DOWN_OUT
  and and_3 (and_3_out, and_1_out, or_1_out);
  or or_1 (or_1_out, and_2_out, WRAP);
  and and_4 (and_4_out, OUTPUT[0], OUTPUT[1], OUTPUT[2], OUTPUT[3], OUTPUT[4], OUTPUT[5], OUTPUT[6], OUTPUT[7], OUTPUT[8], OUTPUT[9], OUTPUT[10], OUTPUT[11], OUTPUT[12], OUTPUT[13], OUTPUT[14], OUTPUT[15]);
  nor nor_1 (ZERO, OUTPUT[0], OUTPUT[1], OUTPUT[2], OUTPUT[3], OUTPUT[4], OUTPUT[5], OUTPUT[6], OUTPUT[7], OUTPUT[8], OUTPUT[9], OUTPUT[10], OUTPUT[11], OUTPUT[12], OUTPUT[13], OUTPUT[14], OUTPUT[15]);
endmodule

module Counter_Cell (
  input  UP_IN,
  input  A,
  input  DOWN_IN,
  input  RESET,
  input  CLOCK,
  output Q,
  output UP_OUT,
  output B,
  output DOWN_OUT
);

  wire t_ff_1_qn;

  T_Flip_Flop t_ff_1 (.T(A), .clk(CLOCK), .Q(Q), .Qn(t_ff_1_qn), .reset(RESET));  // open: preset
  and and_1 (UP_OUT, UP_IN, Q);
  and and_2 (DOWN_OUT, DOWN_IN, t_ff_1_qn);
  or or_1 (B, UP_OUT, DOWN_OUT);
endmodule

module SR_Latch (
  input  S,
  input  R,
  output Q
);

  S_R_Flip_Flop s_r_ff_1 (.Q(Q), .reset(R), .preset(S));  // open: S, R, clk, Qn
endmodule

module Stage_Counter (
  input  CLOCK,
  input  RESET,
  output [1:0] VALUE
);

  J_K_Flip_Flop j_k_ff_1 (.J(1'b1), .K(1'b1), .clk(CLOCK), .Q(VALUE[0]), .reset(RESET));  // open: Qn, preset
  J_K_Flip_Flop j_k_ff_2 (.J(VALUE[0]), .K(VALUE[0]), .clk(CLOCK), .Q(VALUE[1]), .reset(RESET));  // open: Qn, preset
endmodule
